# Fritzing sketch Project Buzzer (saved by Fritzing 0.9.4)
breadboards: 1

parts:
  Arduíno_Uno = Arduino Uno (Rev3)
  RTC_DS3231 = ZS-042 RTC Module
  Buzzer = Piezo Speaker
  R1 = Resistor [tolerance=±5% resistance=470 package="2010 [SMD]"]
  Relé = Keyes Relay [package=THT]
  Interruptor = SWITCH_SPDT [package=kps-1290]
  LED1 = LED - 5mm [color="Red (633nm)" package="5 mm [THT]"]

nets:
  N1: Arduíno_Uno.D11_PWM/MOSI, Relé.ground
  GND: Arduíno_Uno.GND, RTC_DS3231.GND, Buzzer.pin1, Relé.power, Interruptor.S, LED1.cathode
  N2: Arduíno_Uno.A4/SDA, RTC_DS3231.SDA
  N3: Arduíno_Uno.A5/SCL, RTC_DS3231.SCL
  N4: Arduíno_Uno.D3_PWM, LED1.anode
  N5: Arduíno_Uno.D6_PWM, Interruptor.P
  5V: Arduíno_Uno.5V, RTC_DS3231.VCC, Relé.signal, Interruptor.O
  N6: Buzzer.pin2, R1.Pin_1
  N7: R1.Pin_0, Relé.NC

custom parts:
  Keyes Relay: The Keyes 5V relay module is suitable for SCM development, home appliance control. It uses a 5V~12V TIL control signal which can control DC / AC signal.

// code stored in the sketch: Untitled.ino

